# Fritzing sketch PI2 (saved by Fritzing 0.9.3b)
breadboards: 1

parts:
  hc-sr1 = hc-sr04
  U1 = RELAY [package=relay-t9a-2]
  U2 = GAS_SENSOR [package=mq-3]
  PIR1 = PIR sensor
  J2 = Basic Servo
  Componente2 = Arduino Mega 2560 (Rev3)
  J1 = Piezo Speaker
  Display1 = LCD screen 16x2 IIC [part_number=101290]
  Componente3 = Matrix LED de 8x8 basada en MAX7219
  LED1 = LED - 5mm [color="Red (633nm)" package="5 mm [THT]"]
  R1 = Resistor [tolerance=±5% resistance=220 package="2010 [SMD]"]

nets:
  VCC: hc-sr1.VCC, U1.MAIN, U2.B1, PIR1.VDD, J2.vcc, Componente2.5V, Display1.VCC, Componente3.VCC
  N1: hc-sr1.Trig, Componente2.D7_PWM
  N2: hc-sr1.Echo, Componente2.D6_PWM
  GND: hc-sr1.GND, U1.COIL2, U2.A1, PIR1.GND, J2.gnd, Componente2.GND, J1.pin1, Display1.GND, Componente3.GND, R1.Pin_1
  N3: U1.COIL1, Componente2.D8_PWM
  N4: U1.NO, LED1.cathode
  N5: U2.H1, Componente2.D5_PWM
  N6: PIR1.SIG, Componente2.D4_PWM
  N7: J2.pulse, Componente2.D3_PWM
  N8: Componente2.A4, Display1.SDA
  N9: Componente2.A5, Display1.SCL
  N10: Componente2.D2_PWM, J1.pin2
  N11: Componente2.D49, Componente3.DIN
  N12: Componente2.D51, Componente3.CLK
  N13: Componente2.D53, Componente3.CS
  N14: LED1.anode, R1.Pin_0

custom parts:
  LCD screen 16x2 IIC: LCD screen with HD44780 controller enables showing text, symbols, value or anything else that comes from Croduino/Arduino. It is capable of showing 16 symbols in two lines and therefore can be used in many projects that need to send clearly visible and legible output information.. • Color of symbols: White • Backlight: Blue • Dimensions: 80 x 36 x 12 mm • Screen dimensions: 64.5 x 16 mm •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
